# Fritzing sketch DigisparkPro-i2c-RotaryEncoderRGB (saved by Fritzing 0.9.10b)
breadboards: 1

parts:
  SW1 = ENCODER_RGB_CA [package=encoder_led_3]
  C1 = Capacitor [mn=100nF package=cap-pth-5mm]
  C2 = Capacitor [mn=100nF package=cap-pth-5mm]
  R2 = Resistor [tolerance=±5% resistance=220 package="2010 [SMD]"]
  R3 = Resistor [tolerance=±5% resistance=220 package="2010 [SMD]"]
  R4 = Resistor [tolerance=±5% resistance=330 package="2010 [SMD]"]
  Q1 = PNP-Transistor [mpn=BC557 package="TO92 [THT]"]
  Q2 = NPN-Transistor [mpn=BC547 package="TO92 [THT]"]
  R5 = Resistor [tolerance=±5% resistance=1k package="2010 [SMD]"]
  R6 = Resistor [tolerance=±5% resistance=10k package="2010 [SMD]"]
  R7 = Resistor [tolerance=±5% resistance=4.7k package="2010 [SMD]"]
  Componente2 = Digispark Pro
  J1 = screw terminal, 4 pins
  R1 = Resistor [tolerance=±5% resistance=100k package="2010 [SMD]"]

nets:
  N1: SW1.-R, R4.Pin_1
  N2: SW1.-G, R3.Pin_1
  N3: SW1.SW, Componente2.5, R1.Pin_1
  N4: SW1.-B, R2.Pin_1
  N5: SW1.+, Q1.C
  N6: SW1.A, C2.2, Componente2.9
  N7: SW1.B, C1.1, Componente2.11
  N8: SW1.C, C1.2, C2.1, Q2.E, Componente2.GND, J1.pin1, R1.Pin_0
  N9: R2.Pin_0, Componente2.8
  N10: R3.Pin_0, Componente2.3
  N11: R4.Pin_0, Componente2.4
  N12: Q1.E, R6.Pin_0, Componente2.VCC, J1.pin4
  N13: Q1.B, R5.Pin_0, R6.Pin_1
  N14: Q2.B, R7.Pin_0
  N15: Q2.C, R5.Pin_1
  N16: R7.Pin_1, Componente2.10
  N17: Componente2.0, J1.pin3
  N18: Componente2.2, J1.pin2
